# Fritzing sketch SchemaElectStationOled_ArduiProMini (saved by Fritzing 0.9.3b)
circuit board: 8.46667cm x 5.64444cm
perfboards: 1

parts:
  Composant2 = Arduino Pro Mini v13
  T1 = LM35 Temperature Sensor [package="TO92 [THT]"]
  OLED_screen = Grove OLED 128x96
  X1 = USB Connectors [package=usb-a-h]
  U1 = TEMPERATURE-SENSOR [package=to-92]
  R1 = Resistor [tolerance=±5% resistance=4.7k package=THT]
  Composant3 = Real Time Clock Module - DS1307 RTC Breakout Board
  Composant4 = MicroSD Card Module
  S2 = Momentary Switch [package=tactile-pth]
  S3 = Momentary Switch [package=tactile-pth]
  IC1 = Voltage Regulator [package=to-92]

nets:
  VCC: Composant2.VCC, OLED_screen.VCC, U1.VCC, R1.Pin_1, Composant3.5V, Composant4.VCC, IC1.OUT
  GND: Composant2.GND, T1.GND, OLED_screen.GND, X1.GND, U1.GND, Composant3.GND, Composant4.GND, S2.3, S2.4, S3.3, S3.4, IC1.GND
  N1: Composant2.A4, OLED_screen.SCL, Composant3.SDA
  N2: Composant2.A5, OLED_screen.SDA, Composant3.SCL
  N3: Composant2.A0, T1.Vout
  N4: Composant2.D13/SCK, Composant4.SCK
  N5: Composant2.D12/MISO, Composant4.MISO
  N6: Composant2.D11_PWM/MOSI, Composant4.MOSI
  N7: Composant2.D10_PWM/SS, Composant4.CS
  N8: Composant2.D4, S2.1, S2.2
  N9: Composant2.D3_PWM, S3.1, S3.2
  N10: Composant2.D2, U1.ADJ, R1.Pin_0
  N11: T1.+Vs, X1.D+, IC1.IN
